# Fritzing sketch nodemcu_insta_twitter_dht11 (saved by Fritzing 0.9.3b)

parts:
  U1 = NodeMCU V1.0
  Squix1 = OLED 0.96" 128x64 I2C SSD1306
  DHT1 = DHT11 Humitidy and Temperature Sensor

nets:
  N1: U1.D1, Squix1.SCL
  N2: U1.D2, Squix1.SCA
  N3: U1.D3, DHT1.DATA
  3V3: U1.3V3, Squix1.VCC, DHT1.VDD
  GND: U1.GND, Squix1.GND, DHT1.GND

custom parts:
  NodeMCU V1.0: ESP8266 based NodeMCU
  DHT11 Humitidy and Temperature Sensor: DHT11 Humidity and Temperature Sensor
